# Fritzing sketch LedStrip (saved by Fritzing 0.9.3b)
circuit board: 4.3cm x 5.3cm
breadboards: 1

parts:
  ESP8266 = Adafruit HUZZAH ESP8266 [part_number="Adafruit #2471"]
  DC-DC = TracoPower TSR-1 DC/DC Converter [part_number="TSR 1-2450"]
  GND = Header 1 [package=1x01_offset]
  VCC = Header 1 [package=1x01_offset]
  CW_FET = MOSFET-NCHANNEL [package=to220v]
  WW_FET = MOSFET-NCHANNEL [package=to220v]
  R2 = Resistor [tolerance=±5% resistance=220 package=THT]
  Button = Round Pushbutton
  R1 = Resistor [tolerance=±5% resistance=220 package=THT]

nets:
  N1: ESP8266.VIN, DC-DC.3, R2.Pin_0, R1.Pin_0
  N2: ESP8266.GND, DC-DC.2, GND.1, CW_FET.S, WW_FET.S, Button.leg1
  N3: ESP8266.GPIO16, WW_FET.G, R1.Pin_1
  N4: ESP8266.GPIO12, CW_FET.G, R2.Pin_1
  N5: ESP8266.GPIO5, Button.leg0
  N6: DC-DC.1, VCC.1

notes:
  Led Strip 1.0

custom parts:
  Adafruit HUZZAH ESP8266: Add Internet to your next project with an adorable, bite-sized WiFi microcontroller, at a price you like! The ESP8266 processor from Espressif is an 80 MHz microcontroller with a full WiFi front-end (both as client and access point) and TCP/IP stack with DNS support as well. While this chip has been very popular, its also been very difficult to use. Most of the low cost modules are not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
  TracoPower TSR-1 DC/DC Converter: TracoPower TSR 1-2450 DC Converter Input6.5 - 36VDC Max current 1A
